# Fritzing sketch Robosapian (saved by Fritzing 0.9.1b)
circuit board: 8.46667cm x 5.64444cm
breadboards: 4

parts:
  Part1 = Bluetooth HC-05 Macho  # not connected
  Part2 = Arduino Pro Mini v13
  J1 = Basic Servo
  J2 = Basic Servo
  U1 = SWITCH_SPDT [package=kps-1290]
  CAMERA1 = TTL Serial JPEG Camera
  Part5 = SRF05 Ultrasonic Rangefinder
  Part6 = Lilypad Power Supply
  Connector_with_control_board = Header 2 [package=jst-2-smd]
  LED1 = smd LED [color="Red (633nm)" package="0603 [SMD]"]
  Grove3 = Grove Infrared Receiver
  R1 = Resistor [package="2010 [SMD]"]
  Part7 = GY-80

nets:
  GND: Part2.GND, J1.gnd, J2.gnd, CAMERA1.GND, Part5.GND, Part6.GND, Connector_with_control_board.2, LED1.cathode, Grove3.GND, Part7.GND
  N1: Part2.A4, Part7.SDA
  N2: Part2.D13/SCK, Part5.Trig
  N3: Part2.D10_PWM/SS, J2.pulse
  N4: Part2.D9_PWM, J1.pulse
  N5: Part2.D7, R1.Pin_0
  N6: Part2.D5_PWM, U1.O
  N7: Part2.D2, Part5.Echo
  VCC: J1.vcc, Grove3.VCC
  N8: U1.P, Connector_with_control_board.1
  5V: CAMERA1.5V, Part5.VCC, Part6.+, Part7.VCC_IN
  N9: LED1.anode, R1.Pin_1

notes:
  Connection Header to main control board
  IR Reciever
  Pan and Tilt Servos
  Bluetooth
  Module
  Camera
  Inertial measurement unit
  Ultrasonic Sensor
  Arduino Based Controller
  Battery
  Arduino Pro-mini V13
  SPDT Switch

custom parts:
  TTL Serial JPEG Camera: TTL Serial JPEG Camera with NTSC Out
